# Fritzing sketch Board (saved by Fritzing 0.9.4)
circuit board: 3.60563cm x 7.51914cm
breadboards: 1

parts:
  Arduino = Arduino Nano (Rev3.0)
  R1 = Resistor [tolerance=±5% resistance=220 package=THT]
  Ext = Screw terminal - 2 pins [package=THT]
  R2 = Resistor [tolerance=±5% resistance=220 package=THT]
  SD = female pin header, 6 pins [form="♀ (female)"]
  Speaker = female pin header, 4 pins [form="♀ (female)"]
  Power = screw terminal, 2 pins
  J1 = female pin header, 3 pins [form="♀ (female)"]

nets:
  N1: Arduino.GND, Ext.pin2, SD.pin6, Speaker.pin1, Power.pin2
  N2: Arduino.D5, SD.pin2
  N3: Arduino.D8, R1.Pin_0
  N4: Arduino.D9, R2.Pin_0
  N5: Arduino.D11/MOSI, SD.pin3
  N6: Arduino.D12/MISO, SD.pin5
  N7: Arduino.VIN, J1.pin3
  N8: Arduino.3V3, SD.pin1
  N9: Arduino.D13/SCK, SD.pin4
  N10: R1.Pin_1, Speaker.pin4
  N11: Ext.pin1, R2.Pin_1
  N12: Power.pin1, J1.pin2
